// Logisim project e2237691.circ as structural Verilog: 1 circuit, main circuit main
module main (
  input  A1,
  input  A0,
  input  B1,
  input  B0,
  input  S1,
  input  S0,
  output Y0,
  output Y1,
  output Y2,
  output Y3,
  output Y4,
  output Y5,
  output Y6,
  output Y7,
  output X2,
  output X1,
  output X0
);

  wire and_1_out, and_2_out, and_3_out, and_4_out, n4_to_1_mux_x2_74153_1_p9, n4_to_1_mux_x2_74153_2_p3,
       n4_to_1_mux_x2_74153_2_p13, n4_to_1_mux_x2_74153_2_p14, not_1_out, not_2_out, not_3_out, not_4_out,
       or_1_out, or_2_out, or_3_out, or_4_out, xor_1_out;

  not not_1 (not_1_out, A1);
  not not_2 (not_2_out, B1);
  not not_3 (not_3_out, A0);
  not not_4 (not_4_out, B0);
  or or_1 (or_1_out, not_2_out, B0);
  and and_1 (and_1_out, B1, B0);
  or or_2 (or_2_out, not_1_out, B1);
  and and_2 (and_2_out, not_3_out, B0);
  or or_3 (or_3_out, A1, B1);
  and and_3 (and_3_out, or_2_out, and_2_out);
  and and_4 (and_4_out, not_1_out, B1);
  xor xor_1 (xor_1_out, B1, B0);
  // _4_to_1_MUX__x2___74153 #(.Facing("east")) 4_to_1_mux_x2_74153_1: pin names not known; wires that end beside it: B0, or_1_out, and_1_out, 1'b1, 1'b0, A0, 1'b0, A1, n4_to_1_mux_x2_74153_1_p9
  or or_4 (or_4_out, and_3_out, and_4_out);
  // _4_to_1_MUX__x2___74153 #(.Facing("east")) 4_to_1_mux_x2_74153_2: pin names not known; wires that end beside it: xor_1_out, B1, n4_to_1_mux_x2_74153_2_p3, not_2_out, B0, not_4_out, B0, not_4_out, 1'b0, A0, 1'b0, A1, n4_to_1_mux_x2_74153_2_p13, n4_to_1_mux_x2_74153_2_p14
  not not_5 (n4_to_1_mux_x2_74153_2_p3, xor_1_out);
  // _4_to_1_MUX__x2___74153 #(.Facing("east")) 4_to_1_mux_x2_74153_3: pin names not known; wires that end beside it: or_4_out, 1'b0, B1, A1, n4_to_1_mux_x2_74153_2_p13, or_3_out, B0, A0, 1'b0, S0, 1'b0, S1, X2, X1
  // _4_to_1_MUX__x2___74153 #(.Facing("east")) 4_to_1_mux_x2_74153_4: pin names not known; wires that end beside it: n4_to_1_mux_x2_74153_2_p14, n4_to_1_mux_x2_74153_1_p9, 1'b0, 1'b1, 1'b0, S0, S1, X0
  // _3_to_8_decoder__74138 #(.Facing("east")) 3_to_8_decoder_74138_1: pin names not known; wires that end beside it: X0, X1, X2, 1'b1, 1'b0, 1'b0
  // NOT_Gate not_6 has open pins: in=open, out=Y0
  // NOT_Gate not_7 has open pins: in=open, out=Y1
  // NOT_Gate not_8 has open pins: in=open, out=Y2
  // NOT_Gate not_9 has open pins: in=open, out=Y3
  // NOT_Gate not_10 has open pins: in=open, out=Y4
  // NOT_Gate not_11 has open pins: in=open, out=Y5
  // NOT_Gate not_12 has open pins: in=open, out=Y6
  // NOT_Gate not_13 has open pins: in=open, out=Y7

  // Notes on the sheet:
  //   S=11
  //   X2
  //   X1
  //   X0
  //   S=01
  //   X1
  //   X0
  //   X2
  //   S=00
  //   S=10
  //   X1
  //   X0
  //   X2
  //   X1
  //   X0
endmodule
